# Fritzing sketch LoraEmit (saved by Fritzing 0.9.2b)
breadboards: 1

parts:
  Board1 = LORABoard
  Composant1 = Arduino Nano (Rev3.0)

nets:
  N1: Board1.2, Composant1.GND
  N2: Board1.3, Composant1.3V3
  N3: Board1.9, Composant1.D10
  N4: Board1.10, Composant1.D11/MOSI
  N5: Board1.11, Composant1.D12/MISO
  N6: Board1.12, Composant1.D13/SCK

custom parts:
  LORABoard: LORA SX1272 RF Board by Libelium
