# Fritzing sketch Low_Power_With_Led (saved by Fritzing 0.9.2b)
breadboards: 1

parts:
  Composant1 = Arduino Nano (Rev3.0) (ICSP)
  R1 = Resistor [tolerance=±5% resistance=220 package=THT]
  LED1 = LEDs [package=led10mm]

nets:
  N1: Composant1.D4, LED1.C
  N2: Composant1.5V, R1.Pin_0, R1.Pin_1, LED1.A
