# Fritzing sketch LowPowerAndEmitSensors (saved by Fritzing 0.9.2b)
breadboards: 1

parts:
  Board2 = LORABoard
  Composant2 = Arduino Nano (Rev3.0)
  DHT2 = DHT22 Humidity and Temperature Sensor
  Composant3 = SRF05 Ultrasonic Rangefinder
  Board3 = LORABoard

nets:
  GND: Board2.2, Composant2.GND, DHT2.GND, Composant3.GND, Board3.1
  3V3: Board2.3, Composant2.3V3, DHT2.VDD
  N1: Board2.9, Composant2.D10
  N2: Board2.10, Composant2.D11/MOSI
  N3: Board2.11, Composant2.D12/MISO
  N4: Board2.12, Composant2.D13/SCK
  N5: Composant2.D2, DHT2.DATA
  N6: Composant2.D3, Composant3.Echo
  N7: Composant2.D4, Composant3.Trig
  5V: Composant2.5V, Composant3.VCC, Board3.4
  N8: Composant2.A0, Board3.2

custom parts:
  LORABoard: LORA SX1272 RF Board by Libelium
  LORABoard: LORA SX1272 RF Board by Libelium
