# Fritzing sketch ProximitySensor (saved by Fritzing 0.9.2b)
breadboards: 1

parts:
  Composant1 = SRF05 Ultrasonic Rangefinder
  Composant2 = Arduino Nano (Rev3.0)

nets:
  VCC: Composant1.VCC, Composant2.5V
  N1: Composant1.Trig, Composant2.D4
  N2: Composant1.Echo, Composant2.D3
  GND: Composant1.GND, Composant2.GND
